# Fritzing sketch RTC3231 (saved by Fritzing 0.9.2b)
breadboards: 1

parts:
  LCD1 = LCD screen
  Y1 = CRYSTAL [package=crystal-32khz-smd_epson_mc146]
  IC1 = DS1302 [package="SO8 [SMD]"]
  BAT1 = Battery Holders [package=battcon_12mm]
  U2 = POT [package=trim_pot]
  Part1 = Arduino Uno (Rev3)
  R1 = Resistor [tolerance=±5% resistance=1k package=THT]
  S1 = Pushbutton [package="[THT]"]
  R2 = Resistor [tolerance=±5% resistance=220 package=THT]
  S2 = Pushbutton [package="[THT]"]
  R3 = Resistor [tolerance=±5% resistance=220 package=THT]
  S3 = Pushbutton [package="[THT]"]
  R4 = Resistor [tolerance=±5% resistance=220 package=THT]
  R5 = Resistor [tolerance=±5% resistance=220 package=THT]
  J1 = Piezo Speaker

nets:
  VSS: LCD1.VSS, LCD1.E, LCD1.LED-, IC1.0V, BAT1.-, U2.A, Part1.GND, S1.Pin_3, S1.Pin_4, S2.Pin_3, S2.Pin_4, S3.Pin_3, S3.Pin_4, J1.pin1
  VDD: LCD1.VDD, IC1.+V, U2.S, Part1.5V, R1.Pin_1, R2.Pin_1, R3.Pin_1, R4.Pin_1
  N1: LCD1.RS, Part1.D12/MISO
  N2: LCD1.R/W, Part1.D11_PWM/MOSI
  N3: LCD1.DB4, Part1.D5_PWM
  N4: LCD1.DB5, Part1.D4
  N5: LCD1.DB6, Part1.D3_PWM
  N6: LCD1.DB7, Part1.D2
  N7: LCD1.LED+, R1.Pin_0
  N8: Y1.2, IC1.X1_-_Crystal
  N9: Y1.1, IC1.X2_-_Crystal
  N10: IC1.I/O_-_SPI_Data_In/Out, Part1.A4/SDA
  N11: IC1.SCLK_-_SPI_Clock, Part1.A5/SCL
  N12: IC1.Vbat_-_Backup_Supply, BAT1.+
  N13: Part1.D8, S2.Pin_1, S2.Pin_2, R3.Pin_0
  N14: Part1.D9_PWM, S1.Pin_1, S1.Pin_2, R2.Pin_0
  N15: Part1.D10_PWM/SS, R5.Pin_1
  N16: Part1.D7, S3.Pin_1, S3.Pin_2, R4.Pin_0
  N17: R5.Pin_0, J1.pin2

notes:
  RTC 3231 Clock Module
  Made by: David W, Kevin S
